# Fritzing sketch activLoad (saved by Fritzing 0.9.3b)
breadboards: 1

parts:
  Часть1 = Arduino Uno (Rev3)
  M1 = DC Motor
  KY-1 = Keyes Relay [package=THT]

nets:
  N1: Часть1.D7, KY-1.signal
  N2: Часть1.5V, KY-1.power
  N3: Часть1.GND, KY-1.ground
  N4: M1.pin_1, KY-1.NO

custom parts:
  Keyes Relay: The Keyes 5V relay module is suitable for SCM development, home appliance control. It uses a 5V~12V TIL control signal which can control DC / AC signal.

// code stored in the sketch: activeLoad.ino
//???? ?????????? ? ???????? 7
int Relay = 7;

void setup() 
{                
  pinMode(Relay, OUTPUT);     
}

void loop() 
{
  digitalWrite(Relay, LOW);   // ???? ????????
  delay(2000);               
  digitalWrite(Relay, HIGH);  // ???? ?????????
  delay(2000);               
}
