# Fritzing sketch LevelSenserSketch (saved by Fritzing 0.9.3b)
circuit board: 8.46667cm x 5.64444cm
breadboards: 1

parts:
  Часть1 = Arduino Uno (Rev3)
  S1 = Reed switch [package=THT]
  R1 = Resistor [tolerance=±5% resistance=10k package="2512 [SMD]"]

nets:
  N1: Часть1.D3_PWM, S1.pin_2
  N2: Часть1.5V, R1.Pin_0
  N3: Часть1.GND, S1.pin_1, R1.Pin_1

// code stored in the sketch: LevelSensor.ino
// ??? ?????????? ?? Arduino ?????
int ledPin =13;  
// ??? ???????
int sensorPin = 3;

void setup() {
	//??????????????? ????
	pinMode(ledPin, OUTPUT);
	pinMode(sensorPin, INPUT);
}

void loop() {
	//????????? ????????? ???????
	int sensorState =digitalRead(sensorPin);
	if(sensorState==HIGH){
		//???? ?????? ???????, ?? ???? ???? ?????? , ?????????? ?????? ? ???????? ?????? ????????? ?????????????? ???
	}else{
		//?????? ?????????, ????????? ?? ???????? ?????????
	}
	deplay(300);
}
