# Fritzing sketch main (saved by Fritzing 0.9.3b)
breadboards: 1

parts:
  Часть1 = Arduino Uno (Rev3)
  ZS-042_RTC1 = ZS-042 RTC Module
  KY-1 = Keyes Relay [package=THT]
  KY-2 = Keyes Relay [package=THT]
  KY-3 = Keyes Relay [package=THT]
  M2 = DC Motor
  LM1 = RioRand LM2596
  LM2 = RioRand LM2596
  J1 = screw terminal, 3 pins  # not connected
  J2 = screw terminal, 3 pins  # not connected
  J3 = screw terminal, 3 pins
  J4 = screw terminal, 3 pins
  M1 = DC Motor
  J5 = screw terminal, 3 pins
  LED1 = LEDs [package=led-1206]  # not connected
  RHT1 = Humidity and Temperature Sensor RHT03  # not connected
  D1 = SOLAR-IXYS [package=solarbit-12x1]
  R1 = Resistor [tolerance=±5% resistance=220 package=THT]
  LED3_quality = LED - 5mm [color="Red (633nm)" package="5 mm [THT]"]
  R2 = Resistor [tolerance=±5% resistance=220 package=THT]
  LED2_low_level = smd LED [color="Red (633nm)" package="1206 [SMD]"]
  S1 = Reed switch [package=THT]  # not connected
  R3 = Resistor [tolerance=±5% resistance=220 package=THT]
  J6 = screw terminal, 3 pins

nets:
  N1: Часть1.A1, J5.pin2, D1.C
  GND: Часть1.GND, ZS-042_RTC1.GND, KY-1.ground, KY-2.ground, KY-3.ground, LM1.Pin_3, J5.pin3, LED3_quality.cathode, LED2_low_level.cathode, J6.pin1
  N2: Часть1.A4/SDA, ZS-042_RTC1.SDA
  N3: Часть1.A5/SCL, ZS-042_RTC1.SCL
  N4: Часть1.D0/RX, R1.Pin_0
  N5: Часть1.D1/TX, KY-1.signal
  N6: Часть1.D2, KY-2.signal
  N7: Часть1.D3_PWM, KY-3.signal
  N8: Часть1.D4, R2.Pin_1
  N9: Часть1.D5_PWM, R3.Pin_1, J6.pin3
  N10: ZS-042_RTC1.VCC, KY-1.power, KY-2.power, KY-3.power, LM1.Pin_2, R3.Pin_0
  N11: KY-1.NC, KY-2.NC, KY-3.NC, LM2.Pin_2
  N12: KY-1.C, J4.pin2, M1.pin_2
  N13: KY-2.C, M2.pin_2, J3.pin1
  N14: KY-3.C, J3.pin3
  N15: LM2.Pin_3, J3.pin2, J4.pin1, J4.pin3
  N16: LED3_quality.anode, R2.Pin_0

custom parts:
  Keyes Relay: The Keyes 5V relay module is suitable for SCM development, home appliance control. It uses a 5V~12V TIL control signal which can control DC / AC signal.
