# Fritzing sketch Soil_sensor (saved by Fritzing 0.9.3b)
breadboards: 1

parts:
  Часть1 = Arduino Uno (Rev3)
  Часть2 = FC-28 Soil Hygrometer Module
  Часть3 = FC-28 Soil Hygrometer Module - Probe

nets:
  N1: Часть1.A0, Часть2.AO
  5V: Часть1.5V, Часть2.VCC
  GND: Часть1.GND, Часть2.GND
  N2: Часть2.POS, Часть3.NEG
  N3: Часть2.NEG, Часть3.POS

custom parts:
  FC-28 Soil Hygrometer Module: The FC-28 is a soil hygrometer module that uses the Texas Instruments LM393 comparator chip to provide an analog measurement of soil humidity. The digital output is high when soil moisture is over a certain threshold, as determined by adjusting the potentiometer.
  FC-28 Soil Hygrometer Module - Probe: The FC-28 is a soil hygrometer module that uses the Texas Instruments LM393 comparator chip to provide an analog measurement of soil humidity.

// code stored in the sketch: soil_sensor.ino
// ??????? ??????????? ??????????? ?????? ???????
int aPin=A0;
// ???????? ??????????? ??????????? ?????????
int ledPins[8]={4,5,6,7,8,9,10,11};
// ?????????? ??? ?????????? ???????? ???????
int avalue=0;
// ?????????? ?????????? ?????????? ???????????
int countled=8;
// ???????? ??????? ??????
int minvalue=220;
// ???????? ??????????? ???????
int maxvalue=600;

void setup()
{
// ????????????? ????????????????? ?????
Serial.begin(9600);
// ????????? ??????? ????????? ???????????
// ? ????? OUTPUT
for(int i=0;i<8;i++)
{
pinMode(ledPins[i],OUTPUT);
}

}

void loop()
{
// ????????? ???????? ? ??????????? ?????? ???????
avalue=analogRead(aPin);
// ????? ???????? ? ??????? ????????????????? ????? Arduino
Serial.print("avalue=");
Serial.println(avalue);
// ???????????? ???????? ?? 8 ???????????
countled=map(avalue,maxvalue,minvalue,0,7);
// ????????? ?????? ?????????
for(int i=0;i<8;i++)
{
if(i<=countled)
digitalWrite(ledPins[i],HIGH); //???????? ?????????
else
digitalWrite(ledPins[i],LOW); // ????? ?????????
}
// ????? ????? ????????? ?????????? ???????? 1000 ??
delay(1000);
}
