# Fritzing sketch timer (saved by Fritzing 0.9.3b)
breadboards: 1

parts:
  Часть1 = Arduino Uno (Rev3)
  ZS-042_RTC1 = ZS-042 RTC Module

nets:
  N1: Часть1.A4/SDA, ZS-042_RTC1.SDA
  N2: Часть1.A5/SCL, ZS-042_RTC1.SCL
  5V: Часть1.5V, ZS-042_RTC1.VCC
  GND: Часть1.GND, ZS-042_RTC1.GND

// code stored in the sketch: timer.ino
/**
* ??????????:
*  - ???????? ????? ???????? k*30 ??? = k*1600 ???
*  - ????? ?????????? ? ??????? 1 ??? = 60 ??()?
* 
* k ???????????, ??????? ??????? ??: 
* - ??????? ????? (1 ????, 3 ?????)
* - ????????? ( ???????? ?? ??????????? ??????)
*/
#include <Wire.h>
#include "DS3231.h"

#define INTERVAL 	1600
#define PERIOD		60

RTClib RTC;
DS3231 Clock;

int k = 1;


void setup () {
    Serial.begin(9600);
    Wire.begin();
//		Clock.setDate(11);
//		Clock.setHour(7);
//		Clock.setMinute(31);
//		Clock.setDoW(4);
//		Clock.setClockMode(false);
}

void loop () {
  
    delay(1000);
  
    DateTime now = RTC.now();
    
    Serial.print(now.year(), DEC);
    Serial.print('/');
    Serial.print(now.month(), DEC);
    Serial.print('/');
    Serial.print(now.day(), DEC);
    Serial.print(' ');
    Serial.print(now.hour(), DEC);
    Serial.print(':');
    Serial.print(now.minute(), DEC);
    Serial.print(':');
    Serial.print(now.second(), DEC);
    Serial.println();
    
    Serial.print(" since midnight 1/1/1970 = ");
    Serial.print(now.unixtime());
    Serial.print("s = ");
    Serial.print(now.unixtime() / 86400L);
    Serial.println("d");
}
